# Fritzing sketch BoatWiring_protoboard (saved by Fritzing 0.9.10b)
perfboards: 1

parts:
  U1 = atmega328 [package=dip]  # not connected
  Power_plug1 = Power plug  # not connected
  Q1 = Basic FET N-Channel [package="DPak [SMD]"]  # not connected
  Q4 = Basic FET N-Channel [package="DPak [SMD]"]  # not connected
  Q5 = Basic FET N-Channel [package="DPak [SMD]"]  # not connected
  Q6 = Basic FET N-Channel [package="DPak [SMD]"]  # not connected
  Q7 = Basic FET N-Channel [package="DPak [SMD]"]  # not connected
  Q8 = Basic FET N-Channel [package="DPak [SMD]"]  # not connected
  Q9 = Basic FET N-Channel [package="DPak [SMD]"]  # not connected
  Q10 = Basic FET N-Channel [package="DPak [SMD]"]  # not connected
  Q11 = Basic FET N-Channel [package="DPak [SMD]"]  # not connected
  Q12 = Basic FET N-Channel [package="DPak [SMD]"]  # not connected
  Q13 = Basic FET N-Channel [package="DPak [SMD]"]  # not connected
  Q14 = Basic FET N-Channel [package="DPak [SMD]"]  # not connected
  Q15 = Basic FET N-Channel [package="DPak [SMD]"]  # not connected
  Q16 = Basic FET N-Channel [package="DPak [SMD]"]  # not connected
  Q17 = Basic FET N-Channel [package="DPak [SMD]"]  # not connected
  J2 = Camdenboss CTB0158-4 [part_number=CTB0158-4 package=THT]  # not connected
  J3 = Camdenboss CTB0158-4 [part_number=CTB0158-4 package=THT]  # not connected
  J4 = Camdenboss CTB0158-4 [part_number=CTB0158-4 package=THT]  # not connected
  J5 = Camdenboss CTB0158-4 [part_number=CTB0158-4 package=THT]  # not connected
  J6 = Camdenboss CTB0158-4 [part_number=CTB0158-4 package=THT]  # not connected
  C1 = Capacitor [package=cap-pth-small2]
  C2 = Capacitor [package=cap-pth-small2]
  XTAL1 = Crystal [frequency="16 Mhz" package=THT]
  R1 = Resistor [tolerance=±5% power=0.25 resistance=10k package=THT]  # not connected
  U2 = Packages: [package=dil28-3]  # not connected
  R2 = Resistor [tolerance=±5% resistance=2k package="2010 [SMD]"]  # not connected
  J7 = Screw terminal - 2 pins [package=THT]  # not connected
  J8 = Screw terminal - 2 pins [package=THT]  # not connected
  J9 = Screw terminal - 2 pins [package=THT]  # not connected
  J10 = Screw terminal - 2 pins [package=THT]  # not connected
  J11 = Screw terminal - 2 pins [package=THT]  # not connected
  J12 = Screw terminal - 2 pins [package=THT]  # not connected
  J13 = Screw terminal - 2 pins [package=THT]  # not connected
  J14 = Screw terminal - 2 pins [package=THT]  # not connected
  J15 = Screw terminal - 2 pins [package=THT]  # not connected
  J16 = Screw terminal - 2 pins [package=THT]  # not connected
  J17 = Screw terminal - 2 pins [package=THT]  # not connected
  J18 = female pin header, 7 pins [form="♀ (female)"]  # not connected

nets:
  N1: C1.1, XTAL1.pin_1
  N2: C2.2, XTAL1.pin_0
