# Fritzing sketch CarValveCircuit (saved by Fritzing 0.9.3b)
breadboards: 1

parts:
  Part1 = Arduino Uno (Rev3) - ICSP
  S1 = Pushbutton [package="[THT]"]
  U1 = POT [package=pot_mammoth]
  U2 = POT [package=pot_mammoth]
  Q1 = Basic FET P-Channel [package="TO220 [THT]"]
  Q2 = Basic FET P-Channel [package="TO220 [THT]"]
  Power_plug1 = Power plug
  R1 = Resistor [tolerance=±5% resistance=10k package=THT]
  L1 = Inductor [package="400 mil [THT]"]
  L2 = Inductor [package="400 mil [THT]"]

nets:
  N1: Part1.A0, U1.A
  N2: Part1.A1, U2.A
  N3: Part1.D2, Part1.GND, S1.Pin_3, S1.Pin_4, U1.E, U2.E
  N4: Part1.D5_PWM, Q1.gate
  N5: Part1.D6_PWM, Q2.gate
  N6: Part1.5V, U1.S, U2.S, R1.Pin_1
  N7: S1.Pin_1, S1.Pin_2, R1.Pin_0
  N8: Q1.drain, L1.pin_1
  N9: Q1.source, Q2.source, Power_plug1.GND
  N10: Q2.drain, L2.pin_1
  N11: Power_plug1.VCC, L1.pin_0

notes:
  24v DC
